// Logisim project AiAlu.circ as structural Verilog
module ArithUnit (
  input  a0,
  input  a1,
  input  a2,
  input  a3,
  input  a4,
  input  a5,
  input  a6,
  input  a7,
  input  b0,
  input  b1,
  input  b2,
  input  b3,
  input  b4,
  input  b5,
  input  b6,
  input  b7,
  input  [1:0] Operation_Select,
  output [7:0] out_18,
  output out_19
);

  wire button_1_out, operation_selector_1_s1, operation_selector_1_s2, processor_enabler_1_out0,
       processor_enabler_1_out1, processor_enabler_1_out2, processor_enabler_1_out3,
       processor_enabler_1_out4, processor_enabler_1_out5, processor_enabler_1_out6,
       processor_enabler_1_out7, processor_enabler_2_out0, processor_enabler_2_out1,
       processor_enabler_2_out2, processor_enabler_2_out3, processor_enabler_2_out4,
       processor_enabler_2_out5, processor_enabler_2_out6, processor_enabler_2_out7,
       processor_enabler_aux_1_out0, processor_enabler_aux_1_out1, processor_enabler_aux_1_out2,
       processor_enabler_aux_1_out3, processor_enabler_aux_1_out4, processor_enabler_aux_1_out5,
       processor_enabler_aux_1_out6, processor_enabler_aux_1_out7, processor_enabler_aux_2_out0,
       processor_enabler_aux_2_out1, processor_enabler_aux_2_out2, processor_enabler_aux_2_out3,
       processor_enabler_aux_2_out4, processor_enabler_aux_2_out5, processor_enabler_aux_2_out6,
       processor_enabler_aux_2_out7;
  wire [7:0] cpl2_1_y0, intel_adder_inside_1_y0;

  Button button_1 (.out(button_1_out));
  Operation_Selector operation_selector_1 (
    .I0(Operation_Select[0]), .I1(Operation_Select[1]), .S0(out_19), .S1(operation_selector_1_s1),
    .S2(operation_selector_1_s2));  // open: S3
  Processor_Enabler processor_enabler_1 (
    .Processor_Check(operation_selector_1_s1), .IN0(a0), .IN1(a1), .IN2(a2), .IN3(a3), .IN4(a4), .IN5(a5),
    .IN6(a6), .IN7(a7), .OUT0(processor_enabler_1_out0), .OUT1(processor_enabler_1_out1),
    .OUT2(processor_enabler_1_out2), .OUT3(processor_enabler_1_out3), .OUT4(processor_enabler_1_out4),
    .OUT5(processor_enabler_1_out5), .OUT6(processor_enabler_1_out6), .OUT7(processor_enabler_1_out7));
  Intel_Adder_Inside intel_adder_inside_1 (
    .c(button_1_out), .a0(processor_enabler_1_out0), .a1(processor_enabler_1_out1),
    .a2(processor_enabler_1_out2), .a3(processor_enabler_1_out3), .a4(processor_enabler_1_out4),
    .a5(processor_enabler_1_out5), .b0(processor_enabler_aux_1_out0), .a6(processor_enabler_1_out6),
    .b1(processor_enabler_aux_1_out1), .a7(processor_enabler_1_out7), .b2(processor_enabler_aux_1_out2),
    .b4(processor_enabler_aux_1_out4), .b5(processor_enabler_aux_1_out5), .b3(processor_enabler_aux_1_out3),
    .b6(processor_enabler_aux_1_out6), .b7(processor_enabler_aux_1_out7), .y0(intel_adder_inside_1_y0[0]),
    .y1(intel_adder_inside_1_y0[1]), .y2(intel_adder_inside_1_y0[2]), .y3(intel_adder_inside_1_y0[3]),
    .y4(intel_adder_inside_1_y0[4]), .y5(intel_adder_inside_1_y0[5]), .y6(intel_adder_inside_1_y0[6]),
    .y7(intel_adder_inside_1_y0[7]));  // open: Resto
  Processor_Enabler_AUX processor_enabler_aux_1 (
    .Processor_Check(operation_selector_1_s1), .IN0(b0), .IN1(b1), .IN2(b2), .IN3(b3), .IN4(b4), .IN5(b5),
    .IN6(b6), .IN7(b7), .OUT0(processor_enabler_aux_1_out0), .OUT1(processor_enabler_aux_1_out1),
    .OUT2(processor_enabler_aux_1_out2), .OUT3(processor_enabler_aux_1_out3),
    .OUT4(processor_enabler_aux_1_out4), .OUT5(processor_enabler_aux_1_out5),
    .OUT6(processor_enabler_aux_1_out6), .OUT7(processor_enabler_aux_1_out7));
  Processor_Enabler processor_enabler_2 (
    .Processor_Check(operation_selector_1_s2), .IN0(a0), .IN1(a1), .IN2(a2), .IN3(a3), .IN4(a4), .IN5(a5),
    .IN6(a6), .IN7(a7), .OUT0(processor_enabler_2_out0), .OUT1(processor_enabler_2_out1),
    .OUT2(processor_enabler_2_out2), .OUT3(processor_enabler_2_out3), .OUT4(processor_enabler_2_out4),
    .OUT5(processor_enabler_2_out5), .OUT6(processor_enabler_2_out6), .OUT7(processor_enabler_2_out7));
  Cpl2 cpl2_1 (
    .a0(processor_enabler_2_out0), .a1(processor_enabler_2_out1), .a2(processor_enabler_2_out2),
    .a3(processor_enabler_2_out3), .a4(processor_enabler_2_out4), .a5(processor_enabler_2_out5),
    .a6(processor_enabler_2_out6), .a7(processor_enabler_2_out7), .b0(processor_enabler_aux_2_out0),
    .b1(processor_enabler_aux_2_out1), .b2(processor_enabler_aux_2_out2), .b3(processor_enabler_aux_2_out3),
    .b4(processor_enabler_aux_2_out4), .b5(processor_enabler_aux_2_out5), .b6(processor_enabler_aux_2_out6),
    .b7(processor_enabler_aux_2_out7), .y0(cpl2_1_y0[0]), .y1(cpl2_1_y0[1]), .y2(cpl2_1_y0[2]),
    .y3(cpl2_1_y0[3]), .y4(cpl2_1_y0[4]), .y5(cpl2_1_y0[5]), .y6(cpl2_1_y0[6]), .y7(cpl2_1_y0[7]),
    .c(button_1_out));
  Processor_Enabler_AUX processor_enabler_aux_2 (
    .Processor_Check(operation_selector_1_s2), .IN0(b0), .IN1(b1), .IN2(b2), .IN3(b3), .IN4(b4), .IN5(b5),
    .IN6(b6), .IN7(b7), .OUT0(processor_enabler_aux_2_out0), .OUT1(processor_enabler_aux_2_out1),
    .OUT2(processor_enabler_aux_2_out2), .OUT3(processor_enabler_aux_2_out3),
    .OUT4(processor_enabler_aux_2_out4), .OUT5(processor_enabler_aux_2_out5),
    .OUT6(processor_enabler_aux_2_out6), .OUT7(processor_enabler_aux_2_out7));
  Result_Confirmer result_confirmer_1 (
    .a0(intel_adder_inside_1_y0[0]), .a1(intel_adder_inside_1_y0[1]), .a2(intel_adder_inside_1_y0[2]),
    .a3(intel_adder_inside_1_y0[3]), .a4(intel_adder_inside_1_y0[4]), .a5(intel_adder_inside_1_y0[5]),
    .a6(intel_adder_inside_1_y0[6]), .a7(intel_adder_inside_1_y0[7]), .b0(cpl2_1_y0[0]), .b1(cpl2_1_y0[1]),
    .b2(cpl2_1_y0[2]), .b3(cpl2_1_y0[3]), .b4(cpl2_1_y0[4]), .b5(cpl2_1_y0[5]), .b6(cpl2_1_y0[6]),
    .b7(cpl2_1_y0[7]), .out_17(out_18));
endmodule

module Cpl2 (
  input  a0,
  input  a1,
  input  a2,
  input  a3,
  input  a4,
  input  a5,
  input  a6,
  input  a7,
  input  b0,
  input  c,
  input  b1,
  input  b2,
  input  b3,
  input  b4,
  input  b5,
  input  b6,
  input  b7,
  output y0,
  output y1,
  output y2,
  output y3,
  output y4,
  output y5,
  output y6,
  output y7
);

  wire intel_adder_inside_1_resto, intel_adder_inside_1_y0, intel_adder_inside_1_y1, intel_adder_inside_1_y2,
       intel_adder_inside_1_y3, intel_adder_inside_1_y4, intel_adder_inside_1_y5, intel_adder_inside_1_y6,
       intel_adder_inside_1_y7, not_1_out, not_2_out, not_3_out, not_4_out, not_5_out, not_6_out, not_7_out,
       not_8_out;

  not not_1 (not_1_out, b0);
  not not_2 (not_2_out, b1);
  not not_3 (not_3_out, b2);
  not not_4 (not_4_out, b3);
  not not_5 (not_5_out, b4);
  not not_6 (not_6_out, b5);
  not not_7 (not_7_out, b6);
  not not_8 (not_8_out, b7);
  Intel_Adder_Inside intel_adder_inside_1 (
    .c(1'b1), .a0(1'b0), .a1(1'b0), .a2(1'b0), .a3(1'b0), .a4(1'b0), .a5(1'b0), .b0(not_1_out), .a6(1'b0),
    .b1(not_2_out), .a7(1'b0), .b2(not_3_out), .b4(not_5_out), .b5(not_6_out), .b3(not_4_out),
    .b6(not_7_out), .b7(not_8_out), .Resto(intel_adder_inside_1_resto), .y0(intel_adder_inside_1_y0),
    .y1(intel_adder_inside_1_y1), .y2(intel_adder_inside_1_y2), .y3(intel_adder_inside_1_y3),
    .y4(intel_adder_inside_1_y4), .y5(intel_adder_inside_1_y5), .y6(intel_adder_inside_1_y6),
    .y7(intel_adder_inside_1_y7));
  Intel_Adder_Inside intel_adder_inside_2 (
    .c(c), .a0(a0), .a1(a1), .a2(a2), .a3(a3), .a4(a4), .a5(a5), .b0(intel_adder_inside_1_y0), .a6(a6),
    .b1(intel_adder_inside_1_y1), .a7(a7), .b2(intel_adder_inside_1_y2), .b4(intel_adder_inside_1_y4),
    .b5(intel_adder_inside_1_y5), .b3(intel_adder_inside_1_y3), .b6(intel_adder_inside_1_y6),
    .b7(intel_adder_inside_1_y7), .y0(y0), .y1(y1), .y2(y2), .y3(y3), .y4(y4), .y5(y5), .y6(y6), .y7(y7));  // open: Resto
endmodule

module and8bit (
  input  [7:0] aand,
  input  [7:0] band,
  output [7:0] yand
);

  assign yand = aand & band;  // AND_Gate and_1, 8 bits wide
endmodule

module or8bit (
  input  [7:0] aor,
  input  [7:0] bor,
  output [7:0] yor
);

  assign yor = aor | bor;  // OR_Gate or_1, 8 bits wide
endmodule

module not8bit (
  input  [7:0] in_1,
  input  [7:0] in_2
);

  // NOT_Gate not_1 is placed but not wired
endmodule

// Integrated Processor Enabler
module Processor_Enabler (
  input  IN0,
  input  IN1,
  input  IN2,
  input  IN3,
  input  IN4,
  input  IN5,
  input  IN6,
  input  IN7,
  input  Processor_Check,
  output OUT0,
  output OUT1,
  output OUT2,
  output OUT3,
  output OUT4,
  output OUT5,
  output OUT6,
  output OUT7
);

  and and_1 (OUT0, Processor_Check, IN0);
  and and_2 (OUT1, Processor_Check, IN1);
  and and_3 (OUT2, Processor_Check, IN2);
  and and_4 (OUT5, Processor_Check, IN5);
  and and_5 (OUT4, Processor_Check, IN4);
  and and_6 (OUT3, Processor_Check, IN3);
  and and_7 (OUT7, Processor_Check, IN7);
  and and_8 (OUT6, Processor_Check, IN6);
endmodule

// Integrated Processor Enabler
module Processor_Enabler_AUX (
  input  IN0,
  input  IN1,
  input  IN2,
  input  IN3,
  input  IN4,
  input  IN5,
  input  IN6,
  input  IN7,
  input  Processor_Check,
  output OUT0,
  output OUT1,
  output OUT2,
  output OUT3,
  output OUT4,
  output OUT5,
  output OUT6,
  output OUT7
);

  and and_1 (OUT2, Processor_Check, IN2);
  and and_2 (OUT1, Processor_Check, IN1);
  and and_3 (OUT0, Processor_Check, IN0);
  and and_4 (OUT3, Processor_Check, IN3);
  and and_5 (OUT4, Processor_Check, IN4);
  and and_6 (OUT5, Processor_Check, IN5);
  and and_7 (OUT6, Processor_Check, IN6);
  and and_8 (OUT7, Processor_Check, IN7);
endmodule

module Operation_Selector (
  input  I0,
  input  I1,
  output S0,
  output S1,
  output S2,
  output S3
);

  wire not_1_out, not_2_out;

  not not_1 (not_1_out, I0);
  not not_2 (not_2_out, I1);
  and and_1 (S0, not_1_out, not_2_out);
  and and_2 (S1, not_1_out, I1);
  and and_3 (S2, not_2_out, I0);
  and and_4 (S3, I1, I0);
endmodule

// Integrated Result Confirmer
module Result_Confirmer (
  input  a0,
  input  a1,
  input  a2,
  input  a3,
  input  a4,
  input  a5,
  input  a6,
  input  a7,
  input  b0,
  input  b1,
  input  b2,
  input  b3,
  input  b4,
  input  b5,
  input  b6,
  input  b7,
  output [7:0] out_17
);

  or or_1 (out_17[0], a0, b0);
  or or_2 (out_17[1], a1, b1);
  or or_3 (out_17[2], a2, b2);
  or or_4 (out_17[3], a3, b3);
  or or_5 (out_17[4], a4, b4);
  or or_6 (out_17[5], a5, b5);
  or or_7 (out_17[6], a6, b6);
  or or_8 (out_17[7], a7, b7);
endmodule

module Intel_Adder_Inside (
  input  c,
  input  a0,
  input  a1,
  input  a2,
  input  a3,
  input  a4,
  input  a5,
  input  b0,
  input  a6,
  input  b1,
  input  a7,
  input  b2,
  input  b4,
  input  b5,
  input  b3,
  input  b6,
  input  b7,
  output Resto,
  output y0,
  output y1,
  output y2,
  output y3,
  output y4,
  output y5,
  output y6,
  output y7
);

  wire n4_bit_adder_processor_1_c_2;

  _4_bit_adder_processor u_4_bit_adder_processor_1 (
    .c(c), .a0(a0), .a1(a1), .a2(a2), .a3(a3), .b0(b0), .b1(b1), .b2(b2), .b3(b3), .s0(y0), .s1(y1), .s2(y2),
    .s3(y3), .C_2(n4_bit_adder_processor_1_c_2));
  _4_bit_adder_processor u_4_bit_adder_processor_2 (
    .c(n4_bit_adder_processor_1_c_2), .a0(a4), .a1(a5), .a2(a6), .a3(a7), .b0(b4), .b1(b5), .b2(b6), .b3(b7),
    .s0(y4), .s1(y5), .s2(y6), .s3(y7), .C_2(Resto));
endmodule

module Full_Adder_Subsystem (
  input  c0,
  input  a,
  input  b,
  output S,
  output C
);

  wire and_1_out, and_2_out, and_3_out, xor_1_out;

  and and_1 (and_1_out, b, a);
  xor xor_1 (xor_1_out, a, b);
  xor xor_2 (S, xor_1_out, c0);
  and and_2 (and_2_out, c0, a);
  and and_3 (and_3_out, c0, b);
  or or_1 (C, and_1_out, and_2_out, and_3_out);
endmodule

module _4_bit_adder_processor (
  input  c,
  input  a0,
  input  a1,
  input  a2,
  input  a3,
  input  b0,
  input  b1,
  input  b2,
  input  b3,
  output s0,
  output s1,
  output s2,
  output s3,
  output C_2
);

  wire full_adder_subsystem_1_c, full_adder_subsystem_2_c, full_adder_subsystem_3_c;

  Full_Adder_Subsystem full_adder_subsystem_1 (.c0(c), .a(a0), .b(b0), .S(s0), .C(full_adder_subsystem_1_c));
  Full_Adder_Subsystem full_adder_subsystem_2 (
    .c0(full_adder_subsystem_1_c), .a(a1), .b(b1), .S(s1), .C(full_adder_subsystem_2_c));
  Full_Adder_Subsystem full_adder_subsystem_3 (
    .c0(full_adder_subsystem_2_c), .a(a2), .b(b2), .S(s2), .C(full_adder_subsystem_3_c));
  Full_Adder_Subsystem full_adder_subsystem_4 (.c0(full_adder_subsystem_3_c), .a(a3), .b(b3), .S(s3), .C(C_2));
endmodule
